# Fritzing sketch Schema_baudrate (saved by Fritzing 0.8.7b)
breadboards: 1

parts:
  U1 = ESP8266 WiFi Module [part_number=ESP8266]
  Componente2 = Arduino Nano (Rev3.0)

nets:
  N1: U1.RXD, Componente2.D0/RX
  VCC: U1.VCC, U1.RST, U1.CH_PD, Componente2.3V3
  GND: U1.GND, Componente2.GND
  N2: U1.TXD, Componente2.D1/TX

notes:
  ESP8266
  Rx
  Tx
  GND
  VCC (3.3V)
  RST
  CH_PD

custom parts:
  ESP8266 WiFi Module: Generic WiFi Module based on the ESP8266 with onboard PCB antenna and UART communications
