# Fritzing sketch Schema_final (saved by Fritzing 0.8.7b)
breadboards: 1

parts:
  U1 = ESP8266_module [part_number=ESP8266]
  Componente2 = Arduino Nano (Rev3.0)
  LED1 = LEDs [package=led10mm]
  R1 = Resistor [tolerance=±5% resistance=330 package=THT]

nets:
  N1: U1.connector0, Componente2.D2
  N2: U1.connector1, U1.connector3, U1.connector5, Componente2.3V3
  N3: U1.connector6, Componente2.GND, LED1.A
  N4: U1.connector7, Componente2.D3
  N5: Componente2.D5, R1.Pin_0
  N6: LED1.C, R1.Pin_1

notes:
  ESP8266
  Rx
  Tx
  GND
  VCC (3.3V)
  RST
  CH_PD
